# Fritzing sketch breadboard (saved by Fritzing 1.0.3b)
breadboards: 1

parts:
  Mod1 = Raspberry Pi Pico
  U1 = POT [knob_status=50% power=0.5W package=alps_pot]
  U2 = POT [knob_status=50% power=0.5W package=alps_pot]
  U3 = POT [knob_status=50% power=0.5W package=alps_pot]
  U4 = POT [knob_status=50% power=0.5W package=alps_pot]
  U5 = POT [knob_status=50% power=0.5W package=alps_pot]
  Part1 = ADS1015

nets:
  N1: Mod1.pin_3, Mod1.pin_33, Mod1.pin_38, U1.E, U2.E, U3.E, U4.E, U5.E
  N2: Mod1.pin_6, Part1.SDA
  N3: Mod1.pin_7, Part1.SCL
  N4: U1.A, U2.A, U3.A, U4.A, U5.A

custom parts:
  Raspberry Pi Pico: Raspberry Pi Pico. Based around the RP2040 microcontroller the Pico is a low cost microcontroller device bringing Raspberry Pi quality, cost, and easy of use to the microcontroller space. Jan 2021, Split part in to two versions: tht (this one) and SMD. This one will drill holes for a .1 in header in pcb to allow plugging in the module as well as providing pads to solder the module to the top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
  ADS1015: ADC ADS1015
